# Fritzing sketch schematics (saved by Fritzing 0.8.0b)
breadboards: 1

parts:
  Arduino1 = Arduino
  M2 = DC Motor
  M3 = DC Motor
  Onderdeel1 = Arduino Motor Shield
  LED1 = LED - 5mm [color="Red (633nm)" package="5 mm [THT]"]
  LED2 = LED - 5mm [color="Red (633nm)" package="5 mm [THT]"]
  LED3 = LED - 5mm [color="White (6500K)" package="5 mm [THT]"]
  LED4 = LED - 5mm [color="White (6500K)" package="5 mm [THT]"]
  LED5 = LED - 5mm [color="Orange (620nm)" package="5 mm [THT]"]
  LED6 = LED - 5mm [color="Orange (620nm)" package="5 mm [THT]"]
  LED7 = LED - 5mm [color="Orange (620nm)" package="5 mm [THT]"]
  LED8 = LED - 5mm [color="Orange (620nm)" package="5 mm [THT]"]
  LED9 = LED - 5mm [color="Red (633nm)" package="5 mm [THT]"]
  LED10 = LED - 5mm [color="Red (633nm)" package="5 mm [THT]"]
  M1 = DC Motor
  M4 = DC Motor
  J1 = Infrared Proximity Sensor  # not connected
  J2 = Infrared Proximity Sensor  # not connected
  J3 = Infrared Proximity Sensor  # not connected
  Horn = Piezo Speaker
  Powerswitch = Toggle Switch [package=THT]
  VCC1 = 4 x AAA Battery Mount
  Shift_Register_for_LED_lights = 74HC595 [package="DIP16 [THT]"]
  Onderdeel2 = Arduino Motor Shield (Rev3)  # not connected
  Onderdeel4 = Arduino Ethernet Shield (Rev3)  # not connected
  Onderdeel5 = Arduino Wireless SD Shield  # not connected
  Onderdeel6 = Arduino Due (Rev2b)  # not connected

nets:
  N1: Arduino1.aref, Onderdeel1.AREF
  GND: Arduino1.GND, Onderdeel1.GND, Horn.pin1, VCC1.-, Shift_Register_for_LED_lights.GND
  N2: Arduino1.D13, Onderdeel1.D13
  N3: Arduino1.D12, Onderdeel1.D12
  N4: Arduino1.D11, Onderdeel1.D11
  N5: Arduino1.D10, Onderdeel1.D10
  N6: Arduino1.D9, Onderdeel1.D9
  N7: Arduino1.D8, Onderdeel1.D8
  N8: Arduino1.D7, Onderdeel1.D7
  N9: Arduino1.D6, Onderdeel1.D6
  N10: Arduino1.D5, Onderdeel1.D5
  N11: Arduino1.D4, Onderdeel1.D4
  N12: Arduino1.D3, Onderdeel1.D3
  N13: Arduino1.D2, Onderdeel1.D2
  N14: Arduino1.D1TX, Onderdeel1.TX
  N15: Arduino1.D0RX, Onderdeel1.RX
  N16: Arduino1.RST, Onderdeel1.RES
  3V3: Arduino1.3V3, Onderdeel1.3.3V
  +5V: Arduino1.+5V, Onderdeel1.5V, Shift_Register_for_LED_lights.VCC
  VIN: Arduino1.VIN, Onderdeel1.VIN, Powerswitch.COM
  N17: Arduino1.A0, Onderdeel1.A0
  N18: Arduino1.A1, Onderdeel1.A1
  N19: Arduino1.A2, Onderdeel1.A2
  N20: Arduino1.A3, Onderdeel1.A3
  N21: Arduino1.A4, Onderdeel1.A4
  N22: Arduino1.A5, Onderdeel1.A5
  N23: M2.pin_1, M3.pin_2, Onderdeel1.OUT1
  N24: M2.pin_2, M3.pin_1, Onderdeel1.OUT2
  N25: Onderdeel1.OUT3, M1.pin_2, M4.pin_1
  N26: Onderdeel1.OUT4, M1.pin_1, M4.pin_2
  N27: LED1.anode, LED2.cathode
  N28: LED3.anode, LED4.cathode
  N29: LED5.cathode, LED8.anode
  N30: LED6.cathode, LED7.anode
  N31: LED9.anode, LED10.cathode
  N32: Powerswitch.L1, VCC1.+

notes:
  Brake Lights
  Front and backlight
  Turn Left Lights
  Turn Right Lights
  Left Motors
  (Channel B)
  Right Motors
  (Channel A)
  Powersupply
  of some sort
  Left Middle and Right
  Distance sensor IR
  On/Off
  Future LED Driver IC
