# Fritzing sketch schematics (saved by Fritzing 0.7.10b)
breadboards: 1

parts:
  Arduino1 = Arduino
  M1 = DC Motor  # not connected
  M2 = DC Motor  # not connected
  M3 = DC Motor  # not connected
  M4 = DC Motor  # not connected
  Onderdeel1 = Arduino Motor Shield
  VCC1 = Battery

nets:
  N1: Arduino1.aref, Onderdeel1.AREF
  GND: Arduino1.GND, Onderdeel1.GND, VCC1.-
  N2: Arduino1.D13, Onderdeel1.D13
  N3: Arduino1.D12, Onderdeel1.D12
  N4: Arduino1.D11, Onderdeel1.D11
  N5: Arduino1.D10, Onderdeel1.D10
  N6: Arduino1.D9, Onderdeel1.D9
  N7: Arduino1.D8, Onderdeel1.D8
  N8: Arduino1.D7, Onderdeel1.D7
  N9: Arduino1.D6, Onderdeel1.D6
  N10: Arduino1.D5, Onderdeel1.D5
  N11: Arduino1.D4, Onderdeel1.D4
  N12: Arduino1.D3, Onderdeel1.D3
  N13: Arduino1.D2, Onderdeel1.D2
  N14: Arduino1.D1TX, Onderdeel1.TX
  N15: Arduino1.D0RX, Onderdeel1.RX
  N16: Arduino1.RST, Onderdeel1.RES
  3V3: Arduino1.3V3, Onderdeel1.3.3V
  +5V: Arduino1.+5V, Onderdeel1.5V
  VIN: Arduino1.VIN, Onderdeel1.VIN, VCC1.+
  N17: Arduino1.A0, Onderdeel1.A0
  N18: Arduino1.A1, Onderdeel1.A1
  N19: Arduino1.A2, Onderdeel1.A2
  N20: Arduino1.A3, Onderdeel1.A3
  N21: Arduino1.A4, Onderdeel1.A4
  N22: Arduino1.A5, Onderdeel1.A5
